# Fritzing sketch drone_circuit (saved by Fritzing 0.8.5b)
circuit board: 9.5cm x 9.5cm
breadboards: 1

parts:
  M2 = DC Motor
  M3 = DC Motor
  D2 = Diode [package=diode-1n4001]
  JP2 = Header 2 [package=jst-2-pth-kit]
  D3 = Diode [package=diode-1n4001]
  M4 = DC Motor
  D4 = Diode [package=diode-1n4001]
  Part1 = Arduino Pro Mini v13
  D1 = Diode [package=diode-1n4001]
  GY2 = MPU-6050 Board GY-521 [form="♀ (female)" package=THT]
  Q1 = NPN-Transistor [package="TO92 [THT]"]
  M5 = DC Motor
  Q2 = NPN-Transistor [package="TO92 [THT]"]
  Q3 = NPN-Transistor [package="TO92 [THT]"]
  Q4 = NPN-Transistor [package="TO92 [THT]"]
  C1 = Capacitor [package=cap-pth-small-kit]

nets (from the pcb view):
  N1: M2.pin_1, M3.pin_2, D2.A, JP2.1, D3.C, M4.pin_1, D4.C, Part1.VCC, D1.C, GY2.pin1, M5.pin_2, C1.1
  N2: M2.pin_2, D2.C, Q3.C
  N3: M3.pin_1, D1.A, Q2.E
  N4: JP2.2, Part1.GND, GY2.pin2, Q1.E, Q2.C, Q3.E, Q4.E, C1.2
  N5: D3.A, Q1.C, M5.pin_1
  N6: M4.pin_2, D4.A, Q4.C
  N7: Part1.A3, GY2.pin3
  N8: Part1.A2, GY2.pin4
  N9: Part1.A0, Q2.B
  N10: Part1.D10_PWM/SS, Q3.B
  N11: Part1.D5_PWM, Q4.B
  N12: Part1.D4, GY2.pin8
  N13: Part1.D3_PWM, Q1.B

custom parts:
  MPU-6050 Board GY-521: Acelerometro y Giroscopio MPU-6050 Board GY-521
